// Logisim project LC-2200-16.circ as structural Verilog: 5 circuits, main circuit main
module main (
  input  in_1,
  output [15:0] Bus
);

  wire ALUHi, ALULo, Clock, comparator_1_eq, DrALU, DrMEM, DrOFF, DrPC, DrREG, LdA, LdB, LdIR, LdMAR, LdPC,
       LdZ, RegSelHi, RegSelLo, WrMEM, WrREG, Z;
  wire [2:0] OP;
  wire [3:0] regno, zero_1_address;
  wire [12:0] register_5_q;
  wire [15:0] alu_1_answer, bit_extender_1_out, ram_1_data, ram_2_data, register_1_q, register_2_q,
       register_3_q, register_4_q, zero_1_data_out;

  Clock u_Clock (.out(Clock));
  Register #(.width(16)) register_1 (.D(Bus), .en(LdPC), .Q(register_1_q), .clk(Clock), .clr(in_1));
  assign Bus = DrPC ? register_1_q : 16'bz;  // Controlled_Buffer controlled_buffer_1
  Register #(.width(16)) register_2 (.D(Bus), .en(LdA), .Q(register_2_q), .clk(Clock), .clr(in_1));
  Register #(.width(16)) register_3 (.D(Bus), .en(LdB), .Q(register_3_q), .clk(Clock));  // open: clr
  Comparator #(.width(16)) comparator_1 (.a(Bus), .b({16{1'b0}}), .eq(comparator_1_eq));  // open: gt, lt
  ALU alu_1 (.A(register_2_q), .B(register_3_q), .Answer(alu_1_answer), .RegSel({ALUHi, ALULo}));
  assign Bus = DrALU ? alu_1_answer : 16'bz;  // Controlled_Buffer controlled_buffer_2
  Register #(.width(1), .trigger("falling")) Z_register (.D(comparator_1_eq), .en(LdZ), .Q(Z), .clk(Clock), .clr(in_1));
  zero zero_1 (.regno(regno), .Data_in(Bus), .Data_out(zero_1_data_out), .Address(zero_1_address));
  RAM #(.addrWidth(4), .dataWidth(16), .bus("separate")) ram_1 (
    .addr(zero_1_address), .din(zero_1_data_out), .data(ram_1_data), .str(WrREG), .clk(Clock), .clr(in_1));  // open: sel, ld
  assign Bus = DrREG ? ram_1_data : 16'bz;  // Controlled_Buffer controlled_buffer_3
  micro_control_unit micro_control_unit_1 (
    .IR__15_13(OP), .DrREG(DrREG), .DrMEM(DrMEM), .DrALU(DrALU), .DrPC(DrPC), .DrOFF(DrOFF), .LdPC(LdPC),
    .LdIR(LdIR), .LdMAR(LdMAR), .LdA(LdA), .LdB(LdB), .LdZ(LdZ), .WrREG(WrREG), .WrMEM(WrMEM),
    .RegSelLo(RegSelLo), .RegSelHi(RegSelHi), .ALULo(ALULo), .ALUHi(ALUHi), .Clock(Clock), .Z(Z), .Reset(in_1));
  Register #(.width(16)) register_4 (.D(Bus), .en(LdMAR), .Q(register_4_q), .clk(Clock), .clr(in_1));
  Multiplexer #(.select(2), .width(4), .enable("false")) multiplexer_1 (
    .in0(register_5_q[12:9]), .in1(register_5_q[8:5]), .in2(register_5_q[4:1]), .out(regno),
    .sel({RegSelHi, RegSelLo}));  // open: in3
  RAM #(.addrWidth(16), .dataWidth(16), .bus("separate")) ram_2 (
    .addr(register_4_q), .din(Bus), .data(ram_2_data), .str(WrMEM), .clk(Clock));  // open: sel, ld, clr
  assign Bus = DrMEM ? ram_2_data : 16'bz;  // Controlled_Buffer controlled_buffer_4
  Register #(.width(16)) register_5 (.D(Bus), .en(LdIR), .Q({OP, register_5_q}), .clk(Clock), .clr(in_1));
  assign bit_extender_1_out = {{11{register_5_q[4]}}, register_5_q[4:0]};  // Bit_Extender bit_extender_1
  assign Bus = DrOFF ? bit_extender_1_out : 16'bz;  // Controlled_Buffer controlled_buffer_5

  // Other names for the same wires on the sheet: Reset = in_1

  // Notes on the sheet:
  //   SPRING 2016
  //   PC
  //   A
  //   B
  //   MAR
  //   MEMORY
  //   IR
  //   RZ
  //   RX
  //   RY
endmodule

module ALU (
  input  [15:0] A,
  input  [15:0] B,
  input  [1:0] RegSel,
  output [15:0] Answer
);

  wire [15:0] adder_1_out, adder_2_out, nand_1_out, subtractor_1_out;

  Adder #(.width(16)) adder_1 (.a(A), .b(B), .out(adder_1_out));  // open: cin, cout
  assign nand_1_out = ~(A & B);  // NAND_Gate nand_1, 16 bits wide
  Subtractor #(.width(16)) subtractor_1 (.a(A), .b(B), .out(subtractor_1_out));  // open: bin, bout
  Adder #(.width(16)) adder_2 (.a(A), .b(16'h1), .out(adder_2_out));  // open: cin, cout
  Multiplexer #(.select(2), .width(16), .enable("false")) multiplexer_1 (
    .in0(adder_1_out), .in1(nand_1_out), .in2(subtractor_1_out), .in3(adder_2_out), .out(Answer), .sel(RegSel));

  // Notes on the sheet:
  //   ADD
  //   A - B
  //   A + 1
  //   NAND
endmodule

module Register_file (
  input  [15:0] in_1,
  input  [3:0] in_2,
  input  in_3,
  input  clock,
  output [15:0] out_5
);

  wire and_1_out, and_2_out, and_3_out, and_4_out, and_5_out, and_6_out, and_7_out, and_8_out, and_9_out,
       and_10_out, and_11_out, and_12_out, and_13_out, and_14_out, and_15_out, and_16_out, decoder_1_out0,
       decoder_1_out1, decoder_1_out2, decoder_1_out3, decoder_1_out4, decoder_1_out5, decoder_1_out6,
       decoder_1_out7, decoder_1_out8, decoder_1_out9, decoder_1_out10, decoder_1_out11, decoder_1_out12,
       decoder_1_out13, decoder_1_out14, decoder_1_out15;
  wire [15:0] a0, a1, a2, at, fp, k0, ra, s0, s1, s2, sp, t0, t1, t2, v0, zero;

  Multiplexer #(.select(4), .width(16)) multiplexer_1 (
    .in0(zero), .in1(at), .in2(v0), .in3(a0), .in4(a1), .in5(a2), .in6(t0), .in7(t1), .in8(t2), .in9(s0),
    .in10(s1), .in11(s2), .in12(k0), .in13(sp), .in14(fp), .in15(ra), .out(out_5), .sel(in_2));  // open: en
  Decoder #(.select(4)) decoder_1 (
    .out0(decoder_1_out0), .out1(decoder_1_out1), .out2(decoder_1_out2), .out3(decoder_1_out3),
    .out4(decoder_1_out4), .out5(decoder_1_out5), .out6(decoder_1_out6), .out7(decoder_1_out7),
    .out8(decoder_1_out8), .out9(decoder_1_out9), .out10(decoder_1_out10), .out11(decoder_1_out11),
    .out12(decoder_1_out12), .out13(decoder_1_out13), .out14(decoder_1_out14), .out15(decoder_1_out15),
    .sel(in_2));  // open: en
  Register #(.width(16)) register_1 (.D(in_1), .en(and_1_out), .Q(zero), .clk(clock), .clr(1'b1));
  and and_1 (and_1_out, decoder_1_out0, in_3);
  and and_2 (and_2_out, decoder_1_out1, in_3);
  and and_3 (and_3_out, decoder_1_out2, in_3);
  and and_4 (and_4_out, decoder_1_out3, in_3);
  and and_5 (and_5_out, decoder_1_out4, in_3);
  and and_6 (and_6_out, decoder_1_out5, in_3);
  and and_7 (and_7_out, decoder_1_out6, in_3);
  and and_8 (and_8_out, decoder_1_out7, in_3);
  and and_9 (and_9_out, decoder_1_out8, in_3);
  and and_10 (and_10_out, decoder_1_out9, in_3);
  and and_11 (and_11_out, decoder_1_out10, in_3);
  and and_12 (and_12_out, decoder_1_out11, in_3);
  and and_13 (and_13_out, decoder_1_out12, in_3);
  and and_14 (and_14_out, decoder_1_out13, in_3);
  and and_15 (and_15_out, decoder_1_out14, in_3);
  and and_16 (and_16_out, decoder_1_out15, in_3);
  Register #(.width(16)) register_2 (.D(in_1), .en(and_2_out), .Q(at), .clk(clock));  // open: clr
  Register #(.width(16)) register_3 (.D(in_1), .en(and_3_out), .Q(v0), .clk(clock));  // open: clr
  Register #(.width(16)) register_4 (.D(in_1), .en(and_4_out), .Q(a0), .clk(clock));  // open: clr
  Register #(.width(16)) register_5 (.D(in_1), .en(and_5_out), .Q(a1), .clk(clock));  // open: clr
  Register #(.width(16)) register_6 (.D(in_1), .en(and_6_out), .Q(a2), .clk(clock));  // open: clr
  Register #(.width(16)) register_7 (.D(in_1), .en(and_7_out), .Q(t0), .clk(clock));  // open: clr
  Register #(.width(16)) register_8 (.D(in_1), .en(and_8_out), .Q(t1), .clk(clock));  // open: clr
  Register #(.width(16)) register_9 (.D(in_1), .en(and_9_out), .Q(t2), .clk(clock));  // open: clr
  Register #(.width(16)) register_10 (.D(in_1), .en(and_10_out), .Q(s0), .clk(clock));  // open: clr
  Register #(.width(16)) register_11 (.D(in_1), .en(and_11_out), .Q(s1), .clk(clock));  // open: clr
  Register #(.width(16)) register_12 (.D(in_1), .en(and_12_out), .Q(s2), .clk(clock));  // open: clr
  Register #(.width(16)) register_13 (.D(in_1), .en(and_13_out), .Q(k0), .clk(clock));  // open: clr
  Register #(.width(16)) register_14 (.D(in_1), .en(and_14_out), .Q(sp), .clk(clock));  // open: clr
  Register #(.width(16)) register_15 (.D(in_1), .en(and_15_out), .Q(fp), .clk(clock));  // open: clr
  Register #(.width(16)) register_16 (.D(in_1), .en(and_16_out), .Q(ra), .clk(clock));  // open: clr

  // Other names for the same wires on the sheet: Din[15:0] = in_1; Dout[15:0] = out_5; RegSel[3:0] = in_2;
  //   WrREG = in_3
endmodule

module micro_control_unit (
  input  [2:0] IR__15_13,
  input  Z,
  input  Clock,
  input  Reset,
  output DrREG,
  output DrMEM,
  output DrALU,
  output DrPC,
  output DrOFF,
  output LdPC,
  output LdIR,
  output LdMAR,
  output LdA,
  output LdB,
  output LdZ,
  output WrREG,
  output WrMEM,
  output RegSelLo,
  output RegSelHi,
  output ALULo,
  output ALUHi
);

  wire [5:0] multiplexer_1_out, rom_2_data, rom_3_data, State_Register_q;
  wire [24:0] rom_1_data;

  ROM #(.addrWidth(6), .dataWidth(25)) rom_1 (
    .addr(State_Register_q),
    .data({rom_1_data[24:23], ALUHi, ALULo, RegSelHi, RegSelLo, WrMEM, WrREG, LdZ, LdB, LdA, LdMAR, LdIR, LdPC, DrOFF, DrPC, DrALU, DrMEM, DrREG, rom_1_data[5:0]}));  // open: sel
  ROM #(.addrWidth(3), .dataWidth(6)) rom_2 (.addr(IR__15_13), .data(rom_2_data));  // open: sel
  ROM #(.addrWidth(2), .dataWidth(6)) rom_3 (.addr({1'b0, Z}), .data(rom_3_data));  // open: sel
  Multiplexer #(.select(2), .width(6), .enable("false")) multiplexer_1 (
    .in0(rom_1_data[5:0]), .in1(rom_2_data), .in2(rom_3_data), .out(multiplexer_1_out),
    .sel(rom_1_data[24:23]));  // open: in3
  Register #(.width(6)) State_Register (
    .D(multiplexer_1_out), .Q(State_Register_q), .clk(Clock), .clr(Reset));  // open: en

  // Notes on the sheet:
  //   MAIN ROM
  //   Sequencer ROM
  //   Z ROM
  //   contents of rom_1 (hex, n*v repeats v):
  //   6201 1082 e00900 84044 108045 20100 8c047 204108 620100 a020a 840 8404c 840d 210e 20080 84050 8411
  //   2112 40040 84054 8415 20100 4057 88058 1410119 421a 841b 900 1c
  //   contents of rom_2 (hex, n*v repeats v):
  //   3 6 13 b f 16 9 1c
  //   contents of rom_3 (hex, n*v repeats v):
  //   0 19
  //   OpTest
  //   chkZ
  //   NS[5:0]
endmodule

module zero (
  input  [3:0] regno,
  input  [15:0] Data_in,
  output [15:0] Data_out,
  output [3:0] Address
);

  wire nor_1_out, not_1_out;

  nor nor_1 (nor_1_out, regno[3], regno[2], regno[1], regno[0]);
  assign Data_out = nor_1_out ? {16{1'b0}} : 16'bz;  // Controlled_Buffer controlled_buffer_1
  not not_1 (not_1_out, nor_1_out);
  assign Data_out = not_1_out ? Data_in : 16'bz;  // Controlled_Buffer controlled_buffer_2

  assign Address = regno;
endmodule
