// Logisim project control unit.circ as structural Verilog
module micro_control_unit (
  input  [2:0] IR_15_13,
  input  Z,
  output DrREG,
  output DrMEM,
  output DrALU,
  output DrPC,
  output DrOFF,
  output LdPC,
  output LdIR,
  output LdMAR,
  output LdA,
  output LdB,
  output LdZ,
  output WrREG,
  output WrMEM,
  output RegSelLo,
  output RegSelHi,
  output ALULo,
  output ALUHi
);

  wire [5:0] multiplexer_1_out, register_1_q, rom_2_data, rom_3_data;
  wire [24:0] rom_1_data;

  ROM #(.addrWidth(6), .dataWidth(25)) rom_1 (
    .addr(register_1_q),
    .data({rom_1_data[24:23], ALUHi, ALULo, RegSelHi, RegSelLo, WrMEM, WrREG, LdZ, LdB, LdA, LdMAR, LdIR, LdPC, DrOFF, DrPC, DrALU, DrMEM, DrREG, rom_1_data[5:0]}));  // open: sel
  ROM #(.addrWidth(3), .dataWidth(6)) rom_2 (.addr(IR_15_13), .data(rom_2_data));  // open: sel
  ROM #(.addrWidth(2), .dataWidth(6)) rom_3 (.addr({1'b0, Z}), .data(rom_3_data));  // open: sel
  Multiplexer #(.select(2), .width(6)) multiplexer_1 (
    .in0(rom_1_data[5:0]), .in1(rom_2_data), .in2(rom_3_data), .out(multiplexer_1_out), .en(rom_1_data[23]));  // open: in3, sel
  Register #(.width(6)) register_1 (.D(multiplexer_1_out), .Q(register_1_q));  // open: en, clk, clr

  // Notes on the sheet:
  //   MAIN ROM
  //   Sequencer ROM
  //   Z ROM
  //   State Register
  //   NS[5:0]
endmodule
