// Logisim project Mai_Phuc.circ as structural Verilog: 9 circuits, main circuit main
module main (
);

  wire and_1_out, Branch, Clk, Clr, comparator_1_eq, comparator_2_eq, comparator_3_eq, comparator_4_lt,
       comparator_5_eq, comparator_7_gt, comparator_8_lt, comparator_10_gt, comparator_11_eq,
       comparator_12_eq, comparator_13_eq, EN, JALR, NOP, or_1_out, STALL, WB;
  wire [1:0] PC_Sel;
  wire [1:1] comparator_10_eq, comparator_14_eq;
  wire [3:0] idrr_ex_buffer_1_op_code_out, idrr_ex_buffer_1_rx_out, idrr_ex_buffer_1_ry_out, Op_code_EX,
       Op_code_IF, Op_code_MEM, Op_code_WB, REG__2, REG_WB, Rx, Rx_EX, Rx_MEM, Rx_WB, Ry, Ry_EX, Ry_MEM,
       Ry_WB, Rz;
  wire [15:0] Unused;
  wire [23:0] bit_extender_1_out, bit_extender_3_out;
  wire [31:0] adder_2_out, DBUF_A, DBUF_B, Fwrd_OUT1, Fwrd_OUT2, idrr_ex_buffer_1_offset_out,
       idrr_ex_buffer_1_pc_out, idrr_ex_buffer_1_rd_d_1_out, idrr_ex_buffer_1_rd_d_2_out,
       if_idrr_buffer_1_pc_1_out, multiplexer_1_out, multiplexer_12_out, Offset_EX, Offset_IF, Offset_MEM,
       PC, PC_1___Offset_MEM, PC_1_EX, PC_1_MEM, PC___1, PC___1_WB, R_D1_EX, R_D1_MEM, R_D2_EX, R_D2_MEM,
       RAM__WB, Result_EX, Result_MEM, Result_RAM, Result_WB, rom_1_data, WB_Data;

  Clock CLOCK (.out(Clk));
  Register #(.width(32)) u_PC (.D(multiplexer_1_out), .Q(PC), .clk(Clk));  // open: en, clr
  Multiplexer #(.select(2), .width(32), .enable("false")) multiplexer_1 (
    .in0(PC___1), .in1(PC_1___Offset_MEM), .in2(R_D2_MEM), .in3(PC), .out(multiplexer_1_out), .sel(PC_Sel));
  Bit_Extender #(.in_width(32), .out_width(24), .\type ("sign")) bit_extender_1 (.in(PC), .out(bit_extender_1_out));
  Comparator #(.width(4)) comparator_1 (.a(Op_code_EX), .b(4'b0011), .eq(comparator_1_eq));  // open: gt, lt
  Comparator #(.width(4)) comparator_2 (.a(Rx_EX), .b(Ry), .eq(comparator_2_eq));  // open: gt, lt
  Comparator #(.width(4)) comparator_3 (.a(Rx_EX), .b(Rz), .eq(comparator_3_eq));  // open: gt, lt
  Comparator #(.width(4)) comparator_4 (.a(Op_code_IF), .b(4'b0010), .lt(comparator_4_lt));  // open: gt, eq
  Comparator #(.width(4)) comparator_5 (.a(4'b0101), .b(Op_code_MEM), .eq(comparator_5_eq));  // open: gt, lt
  Comparator #(.width(4)) comparator_6 (.a(4'b0110), .b(Op_code_MEM), .eq(PC_Sel[1]));  // open: gt, lt
  Adder #(.width(32)) adder_1 (.a(PC), .b({32{1'b0}}), .out(PC___1), .cin(1'b1));  // open: cout
  and and_1 (and_1_out, comparator_3_eq, comparator_4_lt);
  and and_2 (PC_Sel[0], Branch, comparator_5_eq);
  ROM #(.addrWidth(24), .dataWidth(32)) rom_1 (.addr(bit_extender_1_out), .data(rom_1_data), .sel(EN));
  and and_3 (STALL, comparator_1_eq, or_1_out);
  or or_1 (or_1_out, comparator_2_eq, and_1_out);
  Multiplexer #(.enable("false")) multiplexer_2 (.in0(1'b1), .in1(1'b0), .out(EN), .sel(STALL));
  Register #(.width(1)) register_1 (.D(STALL), .Q(NOP), .clk(Clk));  // open: en, clr
  IF_IDRR_Buffer if_idrr_buffer_1 (
    .En(EN), .Clock(Clk), .Clear(Clr), .PC_1_in(PC___1), .Instr_in(rom_1_data),
    .PC_1_out(if_idrr_buffer_1_pc_1_out), .Instr_out({Op_code_IF, Rx, Ry, Unused, Rz}));
  or or_2 (Clr, PC_Sel[0], PC_Sel[1]);
  Multiplexer #(.width(4), .enable("false")) multiplexer_3 (.in0(Rz), .in1(Rx), .out(REG__2), .sel(comparator_7_gt));
  Comparator #(.width(4)) comparator_7 (.a(Op_code_IF), .b(4'b0010), .gt(comparator_7_gt));  // open: eq, lt
  Comparator #(.width(4)) comparator_8 (.a(Op_code_WB), .b(4'b0100), .lt(comparator_8_lt));  // open: gt, eq
  Comparator #(.width(4)) comparator_9 (.a(Op_code_WB), .b(4'b0110), .eq(JALR));  // open: gt, lt
  Multiplexer #(.width(4), .enable("false")) multiplexer_4 (.in0(Rx_WB), .in1(Ry_WB), .out(REG_WB), .sel(JALR));
  or or_3 (WB, comparator_8_lt, JALR);
  assign Offset_IF = {{12{Unused[15]}}, {Unused, Rz}};  // Bit_Extender bit_extender_2
  IDRR_EX_Buffer idrr_ex_buffer_1 (
    .En(EN), .Clock(Clk), .Clear(Clr), .PC_in(if_idrr_buffer_1_pc_1_out), .R_D_1_in(Fwrd_OUT1),
    .Offset_in(Offset_IF), .R_D_2_in(Fwrd_OUT2), .Op_code_in(Op_code_IF), .Rx_in(Rx), .Ry_in(Ry),
    .PC_out(idrr_ex_buffer_1_pc_out), .Rd_D_1_out(idrr_ex_buffer_1_rd_d_1_out),
    .Offset_out(idrr_ex_buffer_1_offset_out), .Rd_D_2_out(idrr_ex_buffer_1_rd_d_2_out),
    .Op_code_out(idrr_ex_buffer_1_op_code_out), .Rx_out(idrr_ex_buffer_1_rx_out),
    .Ry_out(idrr_ex_buffer_1_ry_out));
  Dual_Ported_Register_File dual_ported_register_file_1 (
    .CLK(Clk), .WrREGNO(REG_WB), .RdREGNO1(Ry), .RdREGNO2(REG__2), .INPUT(WB_Data), .OUT1(DBUF_A),
    .OUT2(DBUF_B), .WrEN(WB));
  Multiplexer #(.width(32), .enable("false")) multiplexer_5 (
    .in0(idrr_ex_buffer_1_pc_out), .in1({32{1'b0}}), .out(PC_1_EX), .sel(NOP));
  Multiplexer #(.width(32), .enable("false")) multiplexer_6 (
    .in0(idrr_ex_buffer_1_rd_d_1_out), .in1({32{1'b0}}), .out(R_D1_EX), .sel(NOP));
  Multiplexer #(.width(32), .enable("false")) multiplexer_7 (
    .in0(idrr_ex_buffer_1_offset_out), .in1({32{1'b0}}), .out(Offset_EX), .sel(NOP));
  Multiplexer #(.width(32), .enable("false")) multiplexer_8 (
    .in0(idrr_ex_buffer_1_rd_d_2_out), .in1({32{1'b0}}), .out(R_D2_EX), .sel(NOP));
  Multiplexer #(.width(4), .enable("false")) multiplexer_9 (
    .in0(idrr_ex_buffer_1_op_code_out), .in1(4'b0000), .out(Op_code_EX), .sel(NOP));
  Multiplexer #(.width(4), .enable("false")) multiplexer_10 (
    .in0(idrr_ex_buffer_1_rx_out), .in1(4'b0000), .out(Rx_EX), .sel(NOP));
  Multiplexer #(.width(4), .enable("false")) multiplexer_11 (
    .in0(idrr_ex_buffer_1_ry_out), .in1(4'b0000), .out(Ry_EX), .sel(NOP));
  Multiplexer #(.width(32), .enable("false")) multiplexer_12 (
    .in0(R_D2_EX), .in1(Offset_EX), .out(multiplexer_12_out), .sel(comparator_10_gt));
  Comparator #(.width(4)) comparator_10 (
    .a(Op_code_EX), .b(4'b0001), .gt(comparator_10_gt), .eq(comparator_10_eq[1]));  // open: lt
  ALU alu_1 (.FUNC({comparator_10_eq[1], 1'b0}), .A(R_D1_EX), .B(multiplexer_12_out), .OUT(Result_EX));
  Forwarding_unit forwarding_unit_1 (
    .EX_Rx(Rx_EX), .EX_OPCODE(Op_code_EX), .MEM_Rx(Rx_MEM), .MEM_OPCODE(Op_code_MEM), .EX_Result(Result_EX),
    .MEM_Result(Result_MEM), .WB_Rx(Rx_WB), .WB_OPCODE(Op_code_WB), .IDRR_Rx(Rx), .IDRR_Ry(Ry),
    .WB_Result(WB_Data), .RAM_Result(Result_RAM), .IDRR_Rz(REG__2), .IDRR_OPCODE(Op_code_IF),
    .IDRR_OUT1(DBUF_A), .IDRR_OUT2(DBUF_B), .Frwd_OUT1(Fwrd_OUT1), .Fwrd_OUT2(Fwrd_OUT2));
  Adder #(.width(32)) adder_2 (.a(PC_1_EX), .b(Offset_EX), .out(adder_2_out));  // open: cin, cout
  Comparator #(.width(32)) comparator_11 (.a(R_D1_EX), .b(R_D2_EX), .eq(comparator_11_eq));  // open: gt, lt
  EX_MEM_Buffer ex_mem_buffer_1 (
    .En(1'b1), .Clock(Clk), .Clear(Clr), .PC___1_in(PC_1_EX), .Rd_D_1_in(R_D1_EX), .Offset_in(Offset_EX),
    .Rd_D_2_in(R_D2_EX), .New_PC_in(adder_2_out), .Result_in(Result_EX), .Op_code_in(Op_code_EX),
    .Rx_in(Rx_EX), .Branch_in(comparator_11_eq), .Ry_in(Ry_EX), .PC___1_out(PC_1_MEM), .Rd_D_1_out(R_D1_MEM),
    .Offset_out(Offset_MEM), .Rd_D_2_out(R_D2_MEM), .New_PC_out(PC_1___Offset_MEM), .Result_out(Result_MEM),
    .Op_code_out(Op_code_MEM), .Rx_out(Rx_MEM), .Branch_out(Branch), .Ry_out(Ry_MEM));
  Bit_Extender #(.in_width(32), .out_width(24), .\type ("sign")) bit_extender_3 (
    .in(Result_MEM), .out(bit_extender_3_out));
  Comparator #(.width(4)) comparator_12 (.a(Op_code_MEM), .b(4'b0100), .eq(comparator_12_eq));  // open: gt, lt
  Comparator #(.width(4)) comparator_13 (.a(4'b0011), .b(Op_code_MEM), .eq(comparator_13_eq));  // open: gt, lt
  RAM #(.addrWidth(24), .dataWidth(32), .bus("separate")) ram_1 (
    .addr(bit_extender_3_out), .din(R_D2_MEM), .data(Result_RAM), .str(comparator_12_eq), .sel(1'b1),
    .clk(Clk), .ld(comparator_13_eq));  // open: clr
  MEM_WB_Buffer mem_wb_buffer_1 (
    .En(1'b1), .Clock(Clk), .Clear(Clr), .PC___1_in(PC_1_MEM), .Result_in(Result_MEM), .RAM_in(Result_RAM),
    .Rx_in(Rx_MEM), .Op_code_in(Op_code_MEM), .Ry_in(Ry_MEM), .PC___1_out(PC___1_WB), .Result_out(Result_WB),
    .RAM_out(RAM__WB), .Rx_out(Rx_WB), .Op_code_out(Op_code_WB), .Ry_out(Ry_WB));
  Comparator #(.width(4)) comparator_14 (.a(Op_code_WB), .b(4'b0011), .eq(comparator_14_eq[1]));  // open: gt, lt
  Multiplexer #(.select(2), .width(32), .enable("false")) multiplexer_13 (
    .in0(Result_WB), .in1(PC___1_WB), .in2(RAM__WB), .out(WB_Data), .sel({comparator_14_eq[1], JALR}));  // open: in3

  // Notes on the sheet:
  //   BEQ?
  //   JALR?
  //   contents of rom_1 (hex, n*v repeats v):
  //   2d00000a 3dd00000 21000007 2300000f 43d00001 61f00000 70000000 37d00001 50000000 6f000000 4000
endmodule

module Dual_Ported_Register_File (
  input  CLK,
  input  WrEN,
  input  [3:0] WrREGNO,
  input  [3:0] RdREGNO1,
  input  [3:0] RdREGNO2,
  input  [31:0] INPUT,
  output [31:0] OUT1,
  output [31:0] OUT2
);

  wire En_a0, En_a1, En_a2, En_a3, En_a4, En_at, En_fp, En_k0, En_ra, En_s0, En_s1, En_s2, En_s3, En_sp,
       En_v0;
  wire [31:0] a0, a1, a2, a3, a4, at, fp, k0, ra, s0, s1, s2, s3, sp, v0, zero;

  Decoder #(.select(4), .disabled(0)) decoder_1 (
    .out1(En_at), .out2(En_v0), .out3(En_a0), .out4(En_a1), .out5(En_a2), .out6(En_a3), .out7(En_a4),
    .out8(En_s0), .out9(En_s1), .out10(En_s2), .out11(En_s3), .out12(En_k0), .out13(En_sp), .out14(En_fp),
    .out15(En_ra), .sel(WrREGNO), .en(WrEN));  // open: out0
  Register #(.width(32)) u_zero (.D(INPUT), .en(1'b0), .Q(zero), .clk(CLK));  // open: clr
  Register #(.width(32)) u_at (.D(INPUT), .en(En_at), .Q(at), .clk(CLK));  // open: clr
  Register #(.width(32)) u_v0 (.D(INPUT), .en(En_v0), .Q(v0), .clk(CLK));  // open: clr
  Register #(.width(32)) u_a0 (.D(INPUT), .en(En_a0), .Q(a0), .clk(CLK));  // open: clr
  Register #(.width(32)) u_a1 (.D(INPUT), .en(En_a1), .Q(a1), .clk(CLK));  // open: clr
  Register #(.width(32)) u_a2 (.D(INPUT), .en(En_a2), .Q(a2), .clk(CLK));  // open: clr
  Register #(.width(32)) u_a3 (.D(INPUT), .en(En_a3), .Q(a3), .clk(CLK));  // open: clr
  Register #(.width(32)) u_a4 (.D(INPUT), .en(En_a4), .Q(a4), .clk(CLK));  // open: clr
  Multiplexer #(.select(4), .width(32), .disabled(0), .enable("false")) multiplexer_1 (
    .in0(zero), .in1(at), .in2(v0), .in3(a0), .in4(a1), .in5(a2), .in6(a3), .in7(a4), .in8(s0), .in9(s1),
    .in10(s2), .in11(s3), .in12(k0), .in13(sp), .in14(fp), .in15(ra), .out(OUT2), .sel(RdREGNO2));
  Register #(.width(32)) u_s0 (.D(INPUT), .en(En_s0), .Q(s0), .clk(CLK));  // open: clr
  Register #(.width(32)) u_s1 (.D(INPUT), .en(En_s1), .Q(s1), .clk(CLK));  // open: clr
  Register #(.width(32)) u_s2 (.D(INPUT), .en(En_s2), .Q(s2), .clk(CLK));  // open: clr
  Register #(.width(32)) u_s3 (.D(INPUT), .en(En_s3), .Q(s3), .clk(CLK));  // open: clr
  Register #(.width(32)) u_k0 (.D(INPUT), .en(En_k0), .Q(k0), .clk(CLK));  // open: clr
  Register #(.width(32)) u_sp (.D(INPUT), .en(En_sp), .Q(sp), .clk(CLK));  // open: clr
  Register #(.width(32)) u_fp (.D(INPUT), .en(En_fp), .Q(fp), .clk(CLK));  // open: clr
  Register #(.width(32)) u_ra (.D(INPUT), .en(En_ra), .Q(ra), .clk(CLK));  // open: clr
  Multiplexer #(.select(4), .width(32), .disabled(0), .enable("false")) multiplexer_2 (
    .in0(zero), .in1(at), .in2(v0), .in3(a0), .in4(a1), .in5(a2), .in6(a3), .in7(a4), .in8(s0), .in9(s1),
    .in10(s2), .in11(s3), .in12(k0), .in13(sp), .in14(fp), .in15(ra), .out(OUT1), .sel(RdREGNO1));

  // Notes on the sheet:
  //   MODIFY AT YOUR OWN RISK
endmodule

// IF/IDRR BUF
module IF_IDRR_Buffer (
  input  En,
  input  Clock,
  input  Clear,
  input  [31:0] PC_1_in,
  input  [31:0] Instr_in,
  output [31:0] PC_1_out,
  output [31:0] Instr_out
);

  wire [31:0] Instr;

  Register #(.width(32)) PC___1 (.D(PC_1_in), .en(En), .Q(PC_1_out), .clk(Clock));  // open: clr
  Multiplexer #(.width(32), .enable("false")) multiplexer_1 (
    .in0(Instr_in), .in1({32{1'b0}}), .out(Instr), .sel(Clear));
  Register #(.width(32)) u_Instr (.D(Instr), .en(En), .Q(Instr_out), .clk(Clock));  // open: clr

  // Other names for the same wires on the sheet: Clk = Clock; Clr = Clear
endmodule

// IDRR/EX BUF
module IDRR_EX_Buffer (
  input  En,
  input  Clock,
  input  Clear,
  input  [31:0] PC_in,
  input  [31:0] R_D_1_in,
  input  [31:0] Offset_in,
  input  [31:0] R_D_2_in,
  input  [3:0] Op_code_in,
  input  [3:0] Rx_in,
  input  [3:0] Ry_in,
  output [31:0] PC_out,
  output [31:0] Rd_D_1_out,
  output [31:0] Offset_out,
  output [31:0] Rd_D_2_out,
  output [3:0] Op_code_out,
  output [3:0] Rx_out,
  output [3:0] Ry_out
);

  wire [3:0] Op_code, Rx, Ry;
  wire [31:0] D_1, D_2, Offset, PC;

  Register #(.width(4)) u_Op_code (.D(Op_code), .en(En), .Q(Op_code_out), .clk(Clock));  // open: clr
  Register #(.width(32)) u_PC (.D(PC), .en(En), .Q(PC_out), .clk(Clock));  // open: clr
  Register #(.width(32)) u_Offset (.D(Offset), .en(En), .Q(Offset_out), .clk(Clock));  // open: clr
  Multiplexer #(.width(32), .enable("false")) multiplexer_1 (.in0(PC_in), .in1({32{1'b0}}), .out(PC), .sel(Clear));
  Multiplexer #(.width(32), .enable("false")) multiplexer_2 (
    .in0(Offset_in), .in1({32{1'b0}}), .out(Offset), .sel(Clear));
  Multiplexer #(.width(4), .enable("false")) multiplexer_3 (
    .in0(Op_code_in), .in1(4'b0000), .out(Op_code), .sel(Clear));
  Multiplexer #(.width(32), .enable("false")) multiplexer_4 (.in0(R_D_1_in), .in1({32{1'b0}}), .out(D_1), .sel(Clear));
  Multiplexer #(.width(32), .enable("false")) multiplexer_5 (.in0(R_D_2_in), .in1({32{1'b0}}), .out(D_2), .sel(Clear));
  Multiplexer #(.width(4), .enable("false")) multiplexer_6 (.in0(Rx_in), .in1(4'b0000), .out(Rx), .sel(Clear));
  Multiplexer #(.width(4), .enable("false")) multiplexer_7 (.in0(Ry_in), .in1(4'b0000), .out(Ry), .sel(Clear));
  Register #(.width(32)) Rd_D_1 (.D(D_1), .en(En), .Q(Rd_D_1_out), .clk(Clock));  // open: clr
  Register #(.width(32)) Rd_D_2 (.D(D_2), .en(En), .Q(Rd_D_2_out), .clk(Clock));  // open: clr
  Register #(.width(4)) u_Rx (.D(Rx), .en(En), .Q(Rx_out), .clk(Clock));  // open: clr
  Register #(.width(4)) u_Ry (.D(Ry), .en(En), .Q(Ry_out), .clk(Clock));  // open: clr

  // Other names for the same wires on the sheet: Clk = Clock; Clr = Clear
endmodule

// EX/MEM BUF
module EX_MEM_Buffer (
  input  En,
  input  Clock,
  input  Clear,
  input  [31:0] PC___1_in,
  input  [31:0] Rd_D_1_in,
  input  [31:0] Offset_in,
  input  [31:0] Rd_D_2_in,
  input  [31:0] New_PC_in,
  input  [31:0] Result_in,
  input  [3:0] Op_code_in,
  input  [3:0] Rx_in,
  input  Branch_in,
  input  [3:0] Ry_in,
  output [31:0] PC___1_out,
  output [31:0] Rd_D_1_out,
  output [31:0] Offset_out,
  output [31:0] Rd_D_2_out,
  output [31:0] New_PC_out,
  output [31:0] Result_out,
  output [3:0] Op_code_out,
  output [3:0] Rx_out,
  output Branch_out,
  output [3:0] Ry_out
);

  wire Branch_in_t, undriven;
  wire [3:0] Op_code_in_t, Rx_in_t, Ry_in_t, undriven_2, undriven_7, undriven_8;
  wire [31:0] New_PC_in_t, Offset_in_t, PC___1_in_t, R_D_2_in, Rd_D_1_in_t, Result_in_t, undriven_3,
       undriven_4, undriven_5, undriven_6, undriven_9, undriven_10, undriven_11;

  Register #(.width(4)) Op_code (.D(Op_code_in), .en(En), .Q(Op_code_out), .clk(Clock));  // open: clr
  Register #(.width(1)) Branch (.D(Branch_in), .en(En), .Q(Branch_out), .clk(Clock));  // open: clr
  Multiplexer #(.width(32), .enable("false")) multiplexer_1 (
    .in0(undriven_4), .in1({32{1'b0}}), .out(PC___1_in_t), .sel(Clear));
  Multiplexer #(.width(32), .enable("false")) multiplexer_2 (
    .in0(undriven_5), .in1({32{1'b0}}), .out(Offset_in_t), .sel(Clear));
  Multiplexer #(.width(32), .enable("false")) multiplexer_3 (
    .in0(undriven_6), .in1({32{1'b0}}), .out(New_PC_in_t), .sel(Clear));
  Multiplexer #(.width(4), .enable("false")) multiplexer_4 (
    .in0(undriven_2), .in1(4'b0000), .out(Op_code_in_t), .sel(Clear));
  Multiplexer #(.enable("false")) multiplexer_5 (.in0(undriven), .in1(1'b0), .out(Branch_in_t), .sel(Clear));
  Register #(.width(32)) PC___1 (.D(PC___1_in), .en(En), .Q(PC___1_out), .clk(Clock));  // open: clr
  Register #(.width(32)) Offset (.D(undriven_3), .en(En), .Q(Offset_out), .clk(Clock));  // open: clr
  Register #(.width(32)) New_PC (.D(New_PC_in), .en(En), .Q(New_PC_out), .clk(Clock));  // open: clr
  Multiplexer #(.width(32), .enable("false")) multiplexer_6 (
    .in0(undriven_9), .in1({32{1'b0}}), .out(Rd_D_1_in_t), .sel(Clear));
  Multiplexer #(.width(32), .enable("false")) multiplexer_7 (
    .in0(undriven_10), .in1({32{1'b0}}), .out(R_D_2_in), .sel(Clear));
  Multiplexer #(.width(32), .enable("false")) multiplexer_8 (
    .in0(undriven_11), .in1({32{1'b0}}), .out(Result_in_t), .sel(Clear));
  Multiplexer #(.width(4), .enable("false")) multiplexer_9 (
    .in0(undriven_7), .in1(4'b0000), .out(Rx_in_t), .sel(Clear));
  Multiplexer #(.width(4), .enable("false")) multiplexer_10 (
    .in0(undriven_8), .in1(4'b0000), .out(Ry_in_t), .sel(Clear));
  Register #(.width(32)) Rd_D_1 (.D(Rd_D_1_in), .en(En), .Q(Rd_D_1_out), .clk(Clock));  // open: clr
  Register #(.width(32)) Rd_D_2 (.D(Rd_D_2_in), .en(En), .Q(Rd_D_2_out), .clk(Clock));  // open: clr
  Register #(.width(32)) Result (.D(Result_in), .en(En), .Q(Result_out), .clk(Clock));  // open: clr
  Register #(.width(4)) Rx (.D(Rx_in), .en(En), .Q(Rx_out), .clk(Clock));  // open: clr
  Register #(.width(4)) Ry (.D(Ry_in), .en(En), .Q(Ry_out), .clk(Clock));  // open: clr

  // Other names for the same wires on the sheet: Clk = Clock; Clr = Clear
endmodule

// MEM/WB BUF
module MEM_WB_Buffer (
  input  En,
  input  Clock,
  input  Clear,
  input  [31:0] PC___1_in,
  input  [31:0] Result_in,
  input  [31:0] RAM_in,
  input  [3:0] Rx_in,
  input  [3:0] Op_code_in,
  input  [3:0] Ry_in,
  output [31:0] PC___1_out,
  output [31:0] Result_out,
  output [31:0] RAM_out,
  output [3:0] Rx_out,
  output [3:0] Op_code_out,
  output [3:0] Ry_out
);

  wire [3:0] Op_code_in_t, Rx_in_t, Ry_in_t, undriven, undriven_5, undriven_6;
  wire [31:0] PC___1_in_t, RAM_in_t, Result_in_t, undriven_2, undriven_3, undriven_4;

  Multiplexer #(.width(4), .enable("false")) multiplexer_1 (
    .in0(undriven), .in1(4'b0000), .out(Op_code_in_t));  // open: sel
  Register #(.width(32)) PC___1 (.D(PC___1_in), .en(En), .Q(PC___1_out), .clk(Clock));  // open: clr
  Register #(.width(32)) RAM (.D(RAM_in), .en(En), .Q(RAM_out), .clk(Clock));  // open: clr
  Register #(.width(4)) Op_code (.D(Op_code_in), .en(En), .Q(Op_code_out), .clk(Clock));  // open: clr
  Multiplexer #(.width(32), .enable("false")) multiplexer_2 (
    .in0(undriven_2), .in1({32{1'b0}}), .out(PC___1_in_t));  // open: sel
  Multiplexer #(.width(32), .enable("false")) multiplexer_3 (
    .in0(undriven_3), .in1({32{1'b0}}), .out(RAM_in_t));  // open: sel
  Multiplexer #(.width(32), .enable("false")) multiplexer_4 (
    .in0(undriven_4), .in1({32{1'b0}}), .out(Result_in_t));  // open: sel
  Multiplexer #(.width(4), .enable("false")) multiplexer_5 (
    .in0(undriven_5), .in1(4'b0000), .out(Rx_in_t));  // open: sel
  Multiplexer #(.width(4), .enable("false")) multiplexer_6 (
    .in0(undriven_6), .in1(4'b0000), .out(Ry_in_t));  // open: sel
  Register #(.width(32)) Result (.D(Result_in), .en(En), .Q(Result_out), .clk(Clock));  // open: clr
  Register #(.width(4)) Rx (.D(Rx_in), .en(En), .Q(Rx_out), .clk(Clock));  // open: clr
  Register #(.width(4)) Ry (.D(Ry_in), .en(En), .Q(Ry_out), .clk(Clock));  // open: clr

  // Other names for the same wires on the sheet: Clk = Clock; Clr = Clear
endmodule

module ALU (
  input  [1:0] FUNC,
  input  [31:0] A,
  input  [31:0] B,
  output [31:0] OUT
);

  wire [31:0] adder_1_out, adder_2_out, nand_1_out, subtractor_1_out;

  Adder #(.width(32)) adder_1 (.a(A), .b(B), .out(adder_1_out), .cin(1'b0));  // open: cout
  assign nand_1_out = ~(A & B);  // NAND_Gate nand_1, 32 bits wide
  Subtractor #(.width(32)) subtractor_1 (.a(A), .b(B), .out(subtractor_1_out), .bin(1'b0));  // open: bout
  Adder #(.width(32)) adder_2 (.a(A), .b({32{1'b0}}), .out(adder_2_out), .cin(1'b1));  // open: cout
  Multiplexer #(.select(2), .width(32), .disabled(0), .enable("false")) multiplexer_1 (
    .in0(adder_1_out), .in1(nand_1_out), .in2(subtractor_1_out), .in3(adder_2_out), .out(OUT), .sel(FUNC));

  // Notes on the sheet:
  //   MODIFY AT YOUR OWN RISK
endmodule

module Forwarding_unit (
  input  [3:0] EX_Rx,
  input  [3:0] EX_OPCODE,
  input  [3:0] MEM_Rx,
  input  [3:0] MEM_OPCODE,
  input  [31:0] EX_Result,
  input  [31:0] MEM_Result,
  input  [3:0] WB_Rx,
  input  [3:0] WB_OPCODE,
  input  [3:0] IDRR_Rx,
  input  [3:0] IDRR_Ry,
  input  [31:0] WB_Result,
  input  [31:0] RAM_Result,
  input  [3:0] IDRR_Rz,
  input  [3:0] IDRR_OPCODE,
  input  [31:0] IDRR_OUT1,
  input  [31:0] IDRR_OUT2,
  output [31:0] Frwd_OUT1,
  output [31:0] Fwrd_OUT2
);

  wire ADD__NAND, comparator_1_lt, comparator_2_eq, comparator_3_lt, comparator_4_eq, comparator_5_lt,
       comparator_6_eq, ENABLE_EX, ENABLE_IDRR_jalr, ENABLE_MEM, ENABLE_WB, EX__Fwrd_Rx, EX__Fwrd_Ry,
       EX__Fwrd_Rz, LW, MEM__Fwrd_Rx, MEM__Fwrd_Ry, MEM__Fwrd_Rz, Rx_bit_0, Rx_bit_1, Rx_bit_2, Rx_bit_3,
       Rx_EX_FORWARD_DPRF_Reg__2, Rx_MEM_FORWARD, Rx_MEM_FORWARD_DPRF_Reg__2, Rx_WB_FORWARD_DPRF_Reg__2,
       Ry_bit_0, Ry_bit_1, Ry_bit_2, Ry_bit_3, Ry_FORWARD_EX_Rx, Ry_FORWARD_MEM_Rx, Ry_FORWARD_WB_Rx,
       Ry_MEM_FORWARD, Rz_bit_0, Rz_bit_1, Rz_bit_2, Rz_bit_3, Rz_FORWARD_EX_Rx, Rz_FORWARD_MEM_Rx,
       Rz_FORWARD_WB_Rx, Rz_MEM_FORWARD, WB__Fwrd_Rx, WB__Fwrd_Ry, WB__Fwrd_Rz;
  wire [1:0] Rx_Sel, Ry_Sel, Rz_Sel, Sel;
  wire [31:0] IDRR_OUT2_t, MEM_Result_t;

  Comparator #(.width(4)) comparator_1 (.a(EX_OPCODE), .b(4'b0100), .lt(comparator_1_lt));  // open: gt, eq
  Comparator #(.width(4)) comparator_2 (.a(EX_OPCODE), .b(4'b0110), .eq(comparator_2_eq));  // open: gt, lt
  Comparator #(.width(4)) comparator_3 (.a(MEM_OPCODE), .b(4'b0100), .lt(comparator_3_lt));  // open: gt, eq
  Comparator #(.width(4)) comparator_4 (.a(MEM_OPCODE), .b(4'b0110), .eq(comparator_4_eq));  // open: gt, lt
  Comparator #(.width(4)) comparator_5 (.a(WB_OPCODE), .b(4'b0100), .lt(comparator_5_lt));  // open: gt, eq
  Comparator #(.width(4)) comparator_6 (.a(WB_OPCODE), .b(4'b0110), .eq(comparator_6_eq));  // open: gt, lt
  Comparator #(.width(4)) comparator_7 (.a(IDRR_OPCODE), .b(4'b0010), .lt(ADD__NAND));  // open: gt, eq
  and and_1 (Rz_FORWARD_EX_Rx, ENABLE_EX, EX__Fwrd_Rz);
  and and_2 (Rz_FORWARD_MEM_Rx, ENABLE_MEM, MEM__Fwrd_Rz);
  and and_3 (Rz_FORWARD_WB_Rx, ENABLE_EX, WB__Fwrd_Rz);
  or or_1 (ENABLE_EX, comparator_1_lt, comparator_2_eq);
  or or_2 (ENABLE_MEM, comparator_3_lt, comparator_4_eq);
  or or_3 (ENABLE_WB, comparator_5_lt, comparator_6_eq);
  Multiplexer #(.select(2), .width(32), .enable("false")) multiplexer_1 (
    .in0(IDRR_OUT2_t), .in1(EX_Result), .in2(MEM_Result_t), .in3(WB_Result), .out(Fwrd_OUT2), .sel(Sel));
  assign Rz_Sel = Rz_bit_0 ? 2'b00 : 2'bz;  // Controlled_Buffer controlled_buffer_1
  assign Rz_Sel = Rz_FORWARD_EX_Rx ? 2'b01 : 2'bz;  // Controlled_Buffer controlled_buffer_2
  assign Rz_Sel = Rz_MEM_FORWARD ? 2'b10 : 2'bz;  // Controlled_Buffer controlled_buffer_3
  assign Rz_Sel = Rz_bit_1 ? 2'b11 : 2'bz;  // Controlled_Buffer controlled_buffer_4
  or or_4 (Rz_MEM_FORWARD, Rz_bit_2, Rz_bit_3);
  Comparator #(.width(4)) comparator_8 (.a(IDRR_Ry), .b(MEM_Rx), .eq(MEM__Fwrd_Ry));  // open: gt, lt
  Comparator #(.width(4)) comparator_9 (.a(IDRR_Rz), .b(MEM_Rx), .eq(MEM__Fwrd_Rz));  // open: gt, lt
  Comparator #(.width(4)) comparator_10 (.a(IDRR_Ry), .b(WB_Rx), .eq(WB__Fwrd_Ry));  // open: gt, lt
  Comparator #(.width(4)) comparator_11 (.a(IDRR_Rz), .b(WB_Rx), .eq(WB__Fwrd_Rz));  // open: gt, lt
  Comparator #(.width(4)) comparator_12 (.a(IDRR_Ry), .b(EX_Rx), .eq(EX__Fwrd_Ry));  // open: gt, lt
  Comparator #(.width(4)) comparator_13 (.a(IDRR_Rz), .b(EX_Rx), .eq(EX__Fwrd_Rz));  // open: gt, lt
  and and_4 (Ry_FORWARD_EX_Rx, ENABLE_EX, EX__Fwrd_Ry);
  and and_5 (Ry_FORWARD_MEM_Rx, ENABLE_MEM, MEM__Fwrd_Ry);
  and and_6 (Ry_FORWARD_WB_Rx, ENABLE_EX, WB__Fwrd_Ry);
  Comparator #(.width(3)) comparator_14 (
    .a({Rz_FORWARD_EX_Rx, Rz_FORWARD_MEM_Rx, Rz_FORWARD_WB_Rx}), .b(3'b000), .eq(Rz_bit_0));  // open: gt, lt
  Comparator #(.width(3)) comparator_15 (
    .a({Rz_FORWARD_EX_Rx, Rz_FORWARD_MEM_Rx, Rz_FORWARD_WB_Rx}), .b(3'b001), .eq(Rz_bit_1));  // open: gt, lt
  Comparator #(.width(3)) comparator_16 (
    .a({Rz_FORWARD_EX_Rx, Rz_FORWARD_MEM_Rx, Rz_FORWARD_WB_Rx}), .b(3'b010), .eq(Rz_bit_2));  // open: gt, lt
  Comparator #(.width(3)) comparator_17 (
    .a({Rz_FORWARD_EX_Rx, Rz_FORWARD_MEM_Rx, Rz_FORWARD_WB_Rx}), .b(3'b011), .eq(Rz_bit_3));  // open: gt, lt
  Multiplexer #(.width(32), .enable("false")) multiplexer_2 (
    .in0(MEM_Result), .in1(RAM_Result), .out(MEM_Result_t), .sel(LW));
  Multiplexer #(.select(2), .width(32), .enable("false")) multiplexer_3 (
    .in0(IDRR_OUT1), .in1(EX_Result), .in2(MEM_Result_t), .in3(WB_Result), .out(Frwd_OUT1), .sel(Ry_Sel));
  Comparator #(.width(3)) comparator_18 (
    .a({Ry_FORWARD_EX_Rx, Ry_FORWARD_MEM_Rx, Ry_FORWARD_WB_Rx}), .b(3'b000), .eq(Ry_bit_0));  // open: gt, lt
  Comparator #(.width(3)) comparator_19 (
    .a({Ry_FORWARD_EX_Rx, Ry_FORWARD_MEM_Rx, Ry_FORWARD_WB_Rx}), .b(3'b001), .eq(Ry_bit_1));  // open: gt, lt
  Comparator #(.width(3)) comparator_20 (
    .a({Ry_FORWARD_EX_Rx, Ry_FORWARD_MEM_Rx, Ry_FORWARD_WB_Rx}), .b(3'b010), .eq(Ry_bit_2));  // open: gt, lt
  Comparator #(.width(3)) comparator_21 (
    .a({Ry_FORWARD_EX_Rx, Ry_FORWARD_MEM_Rx, Ry_FORWARD_WB_Rx}), .b(3'b011), .eq(Ry_bit_3));  // open: gt, lt
  Comparator #(.width(4)) comparator_22 (.a(IDRR_OPCODE), .b(4'b0110), .eq(ENABLE_IDRR_jalr));  // open: gt, lt
  Comparator #(.width(4)) comparator_23 (.a(IDRR_Rx), .b(MEM_Rx), .eq(MEM__Fwrd_Rx));  // open: gt, lt
  Comparator #(.width(4)) comparator_24 (.a(IDRR_Rx), .b(WB_Rx), .eq(WB__Fwrd_Rx));  // open: gt, lt
  Comparator #(.width(4)) comparator_25 (.a(IDRR_Rx), .b(EX_Rx), .eq(EX__Fwrd_Rx));  // open: gt, lt
  and and_7 (Rx_EX_FORWARD_DPRF_Reg__2, ENABLE_IDRR_jalr, EX__Fwrd_Rx);
  and and_8 (Rx_MEM_FORWARD_DPRF_Reg__2, ENABLE_IDRR_jalr, MEM__Fwrd_Rx);
  and and_9 (Rx_WB_FORWARD_DPRF_Reg__2, ENABLE_IDRR_jalr, WB__Fwrd_Rx);
  Comparator #(.width(4)) comparator_26 (.a(MEM_OPCODE), .b(4'b0100), .eq(LW));  // open: gt, lt
  assign Ry_Sel = Ry_bit_0 ? 2'b00 : 2'bz;  // Controlled_Buffer controlled_buffer_5
  assign Ry_Sel = Ry_FORWARD_EX_Rx ? 2'b01 : 2'bz;  // Controlled_Buffer controlled_buffer_6
  assign Ry_Sel = Ry_MEM_FORWARD ? 2'b10 : 2'bz;  // Controlled_Buffer controlled_buffer_7
  assign Ry_Sel = Ry_bit_1 ? 2'b11 : 2'bz;  // Controlled_Buffer controlled_buffer_8
  or or_5 (Ry_MEM_FORWARD, Ry_bit_2, Ry_bit_3);
  Multiplexer #(.width(2), .enable("false")) multiplexer_4 (
    .in0(Rz_Sel), .in1(Rx_Sel), .out(Sel), .sel(ENABLE_IDRR_jalr));
  or or_6 (Rx_MEM_FORWARD, Rx_bit_2, Rx_bit_3);
  Comparator #(.width(3)) comparator_27 (
    .a({Rx_EX_FORWARD_DPRF_Reg__2, Rx_MEM_FORWARD_DPRF_Reg__2, Rx_WB_FORWARD_DPRF_Reg__2}), .b(3'b000),
    .eq(Rx_bit_0));  // open: gt, lt
  Comparator #(.width(3)) comparator_28 (
    .a({Rx_EX_FORWARD_DPRF_Reg__2, Rx_MEM_FORWARD_DPRF_Reg__2, Rx_WB_FORWARD_DPRF_Reg__2}), .b(3'b001),
    .eq(Rx_bit_1));  // open: gt, lt
  Comparator #(.width(3)) comparator_29 (
    .a({Rx_EX_FORWARD_DPRF_Reg__2, Rx_MEM_FORWARD_DPRF_Reg__2, Rx_WB_FORWARD_DPRF_Reg__2}), .b(3'b010),
    .eq(Rx_bit_2));  // open: gt, lt
  Comparator #(.width(3)) comparator_30 (
    .a({Rx_EX_FORWARD_DPRF_Reg__2, Rx_MEM_FORWARD_DPRF_Reg__2, Rx_WB_FORWARD_DPRF_Reg__2}), .b(3'b011),
    .eq(Rx_bit_3));  // open: gt, lt
  assign Rx_Sel = Rx_bit_0 ? 2'b00 : 2'bz;  // Controlled_Buffer controlled_buffer_9
  assign Rx_Sel = Rx_EX_FORWARD_DPRF_Reg__2 ? 2'b01 : 2'bz;  // Controlled_Buffer controlled_buffer_10
  assign Rx_Sel = Rx_MEM_FORWARD_DPRF_Reg__2 ? 2'b10 : 2'bz;  // Controlled_Buffer controlled_buffer_11
  assign Rx_Sel = Rx_bit_1 ? 2'b11 : 2'bz;  // Controlled_Buffer controlled_buffer_12
endmodule

module zero_register (
  input  [31:0] D_in
);
endmodule
